# Fritzing sketch RFID (saved by Fritzing 0.9.3b)

parts:
  K1 = Relay [part_number=FRS1B-S package=THT]
  Part1 = Arduino Nano (Rev3.0)
  U1 = mystery part, 2 pins [chip_label=PORTAO]
  U2 = mystery part, 2 pins [chip_label="12VAC PWR SUPPLY CENTRAL"]
  U3 = mystery part, 2 pins [chip_label="12VAC PWR SUPPLY 2"]
  U4 = mystery part, 6 pins [chip_label="RFID READER"]
  U5 = mystery part, 3 pins [chip_label="IR RECV"]

nets:
  N1: K1.A, U2.pin1
  N2: K1.COIL1, Part1.D6
  N3: K1.C2, U1.pin1
  N4: K1.COIL2, Part1.GND, U4.pin2, U5.pin3
  N5: K1.B, U3.pin1
  N6: Part1.D2, U4.pin3
  N7: Part1.D3, U4.pin4
  N8: Part1.D4, U4.pin5
  N9: Part1.D5, U4.pin6
  N10: Part1.D9, U5.pin2
  N11: Part1.VIN, U4.pin1
  N12: Part1.5V, U5.pin1
  N13: U1.pin2, U2.pin2, U3.pin2
